// Logisim project flipplop.circ as structural Verilog: 4 circuits, main circuit main
module main (
);

  wire clock_1_out, tiktac0_59_1_prox, tiktac0_59_2_prox;
  wire [3:0] h1, h2, m1, m2, s1, s2;

  Hex_Digit_Display hex_digit_display_1 (.value(h1));  // open: dp
  Hex_Digit_Display hex_digit_display_2 (.value(h2));  // open: dp
  Hex_Digit_Display hex_digit_display_3 (.value(m1));  // open: dp
  Hex_Digit_Display hex_digit_display_4 (.value(m2));  // open: dp
  Hex_Digit_Display hex_digit_display_5 (.value(s1));  // open: dp
  Hex_Digit_Display hex_digit_display_6 (.value(s2));  // open: dp
  tiktac0_23 tiktac0_23_1 (.CLK(tiktac0_59_1_prox), .dir(h2), .esq(h1));
  tiktac0_59 tiktac0_59_1 (.CLK(tiktac0_59_2_prox), .dir(m2), .esq(m1), .prox(tiktac0_59_1_prox));
  Clock clock_1 (.out(clock_1_out));
  tiktac0_59 tiktac0_59_2 (.CLK(clock_1_out), .dir(s2), .esq(s1), .prox(tiktac0_59_2_prox));
endmodule

module aula (
);

  wire and_1_out, and_2_out, clock_1_out, clock_2_out, clock_3_out, clock_4_out;
  wire [3:0] t_ff_1_q, t_ff_2_q, t_ff_3_q, t_ff_3_qn, t_ff_13_q, t_ff_14_q;

  Clock clock_1 (.out(clock_1_out));
  Clock clock_2 (.out(clock_2_out));
  Clock clock_3 (.out(clock_3_out));
  T_Flip_Flop #(.trigger("falling")) t_ff_1 (
    .clk(clock_1_out), .T(1'b1), .Q(t_ff_1_q[0]));  // open: Qn, preset, reset, en
  T_Flip_Flop t_ff_2 (.clk(clock_2_out), .T(1'b1), .Q(t_ff_2_q[0]));  // open: Qn, preset, reset, en
  T_Flip_Flop #(.trigger("falling")) t_ff_3 (
    .clk(clock_3_out), .T(1'b1), .Q(t_ff_3_q[0]), .Qn(t_ff_3_qn[0]));  // open: preset, reset, en
  Hex_Digit_Display hex_digit_display_1 (.value(t_ff_3_q));  // open: dp
  T_Flip_Flop #(.trigger("falling")) t_ff_4 (
    .clk(t_ff_1_q[0]), .T(1'b1), .Q(t_ff_1_q[1]));  // open: Qn, preset, reset, en
  T_Flip_Flop t_ff_5 (.clk(t_ff_2_q[0]), .T(1'b1), .Q(t_ff_2_q[1]));  // open: Qn, preset, reset, en
  T_Flip_Flop #(.trigger("falling")) t_ff_6 (
    .clk(t_ff_3_q[0]), .T(1'b1), .Q(t_ff_3_q[1]), .Qn(t_ff_3_qn[1]));  // open: preset, reset, en
  T_Flip_Flop #(.trigger("falling")) t_ff_7 (
    .clk(t_ff_1_q[1]), .T(1'b1), .Q(t_ff_1_q[2]));  // open: Qn, preset, reset, en
  T_Flip_Flop t_ff_8 (.clk(t_ff_2_q[1]), .T(1'b1), .Q(t_ff_2_q[2]));  // open: Qn, preset, reset, en
  T_Flip_Flop #(.trigger("falling")) t_ff_9 (
    .clk(t_ff_3_q[1]), .T(1'b1), .Q(t_ff_3_q[2]), .Qn(t_ff_3_qn[2]));  // open: preset, reset, en
  T_Flip_Flop #(.trigger("falling")) t_ff_10 (
    .clk(t_ff_1_q[2]), .T(1'b1), .Q(t_ff_1_q[3]));  // open: Qn, preset, reset, en
  Hex_Digit_Display hex_digit_display_2 (.value(t_ff_1_q));  // open: dp
  T_Flip_Flop t_ff_11 (.clk(t_ff_2_q[2]), .T(1'b1), .Q(t_ff_2_q[3]));  // open: Qn, preset, reset, en
  Hex_Digit_Display hex_digit_display_3 (.value(t_ff_2_q));  // open: dp
  T_Flip_Flop #(.trigger("falling")) t_ff_12 (
    .clk(t_ff_3_q[2]), .T(1'b1), .Q(t_ff_3_q[3]), .Qn(t_ff_3_qn[3]));  // open: preset, reset, en
  Hex_Digit_Display hex_digit_display_4 (.value(t_ff_3_qn));  // open: dp
  Clock clock_4 (.out(clock_4_out));
  T_Flip_Flop #(.trigger("falling")) t_ff_13 (
    .clk(clock_4_out), .T(1'b1), .Q(t_ff_13_q[0]), .reset(and_1_out));  // open: Qn, preset, en
  and and_1 (and_1_out, t_ff_13_q[3], ~t_ff_13_q[2], t_ff_13_q[1], ~t_ff_13_q[0]);  // AND_Gate
  T_Flip_Flop #(.trigger("falling")) t_ff_14 (
    .clk(and_1_out), .T(1'b1), .Q(t_ff_14_q[0]), .reset(and_2_out));  // open: Qn, preset, en
  and and_2 (and_2_out, ~t_ff_14_q[3], t_ff_14_q[2], t_ff_14_q[1], ~t_ff_14_q[0]);  // AND_Gate
  T_Flip_Flop #(.trigger("falling")) t_ff_15 (
    .clk(t_ff_13_q[0]), .T(1'b1), .Q(t_ff_13_q[1]), .reset(and_1_out));  // open: Qn, preset, en
  T_Flip_Flop #(.trigger("falling")) t_ff_16 (
    .clk(t_ff_14_q[0]), .T(1'b1), .Q(t_ff_14_q[1]), .reset(and_2_out));  // open: Qn, preset, en
  T_Flip_Flop #(.trigger("falling")) t_ff_17 (
    .clk(t_ff_13_q[1]), .T(1'b1), .Q(t_ff_13_q[2]), .reset(and_1_out));  // open: Qn, preset, en
  T_Flip_Flop #(.trigger("falling")) t_ff_18 (
    .clk(t_ff_14_q[1]), .T(1'b1), .Q(t_ff_14_q[2]), .reset(and_2_out));  // open: Qn, preset, en
  Hex_Digit_Display hex_digit_display_5 (.value(t_ff_14_q));  // open: dp
  T_Flip_Flop #(.trigger("falling")) t_ff_19 (
    .clk(t_ff_13_q[2]), .T(1'b1), .Q(t_ff_13_q[3]), .reset(and_1_out));  // open: Qn, preset, en
  Hex_Digit_Display hex_digit_display_6 (.value(t_ff_13_q));  // open: dp
  T_Flip_Flop #(.trigger("falling")) t_ff_20 (
    .clk(t_ff_14_q[2]), .T(1'b1), .Q(t_ff_14_q[3]), .reset(and_2_out));  // open: Qn, preset, en
  Hex_Digit_Display hex_digit_display_7 (.value(t_ff_14_q));  // open: dp
  Hex_Digit_Display hex_digit_display_8 (.value(t_ff_13_q));  // open: dp
endmodule

module tiktac0_23 (
  input  CLK,
  output [3:0] dir,
  output [3:0] esq
);

  wire ifelse, reset3, reset4, reset10, where2;

  Hex_Digit_Display hex_digit_display_1 (.value({1'b0, esq[2:0]}));  // open: dp
  Hex_Digit_Display hex_digit_display_2 (.value(dir));  // open: dp
  T_Flip_Flop #(.trigger("falling")) t_ff_1 (.clk(CLK), .T(1'b1), .Q(dir[0]), .reset(ifelse));  // open: Qn, preset, en
  T_Flip_Flop #(.trigger("falling")) t_ff_2 (
    .clk(ifelse), .T(1'b1), .Q(esq[0]), .reset(reset3));  // open: Qn, preset, en
  T_Flip_Flop #(.trigger("falling")) t_ff_3 (
    .clk(dir[0]), .T(1'b1), .Q(dir[1]), .reset(ifelse));  // open: Qn, preset, en
  T_Flip_Flop #(.trigger("falling")) t_ff_4 (
    .clk(esq[0]), .T(1'b1), .Q(esq[1]), .reset(reset3));  // open: Qn, preset, en
  T_Flip_Flop #(.trigger("falling")) t_ff_5 (
    .clk(dir[1]), .T(1'b1), .Q(dir[2]), .reset(ifelse));  // open: Qn, preset, en
  T_Flip_Flop #(.trigger("falling")) t_ff_6 (
    .clk(esq[1]), .T(1'b1), .Q(esq[2]), .reset(reset3));  // open: Qn, preset, en
  T_Flip_Flop #(.trigger("falling")) t_ff_7 (
    .clk(dir[2]), .T(1'b1), .Q(dir[3]), .reset(ifelse));  // open: Qn, preset, en
  and and_1 (reset10, ~dir[0], dir[1], ~dir[2], dir[3]);  // AND_Gate
  and and_2 (reset4, ~dir[0], ~dir[1], dir[2], ~dir[3]);  // AND_Gate
  and and_3 (reset3, esq[0], esq[1], ~esq[2], ~1'b0);  // AND_Gate
  and and_4 (where2, ~esq[0], esq[1], ~esq[2], ~1'b0);  // AND_Gate
  Multiplexer #(.enable("false")) multiplexer_1 (.in0(reset10), .in1(reset4), .out(ifelse), .sel(where2));

  assign esq[3] = 1'b0;

  // Other names for the same wires on the sheet: b0_t = dir[0]; dist1[3:0] = dir; b1_t = dir[1]; b2_t = dir[2];
  //   b3 = dir[3]; B0 = esq[0]; dist2[2:0] = esq[2:0]; B1 = esq[1]; B2 = esq[2]
endmodule

module tiktac0_59 (
  input  CLK,
  output [3:0] dir,
  output prox,
  output [3:0] esq
);

  wire reset10;

  Hex_Digit_Display hex_digit_display_1 (.value(esq));  // open: dp
  Hex_Digit_Display hex_digit_display_2 (.value(dir));  // open: dp
  T_Flip_Flop #(.trigger("falling")) t_ff_1 (.clk(CLK), .T(1'b1), .Q(dir[0]), .reset(reset10));  // open: Qn, preset, en
  T_Flip_Flop #(.trigger("falling")) t_ff_2 (
    .clk(reset10), .T(1'b1), .Q(esq[0]), .reset(prox));  // open: Qn, preset, en
  T_Flip_Flop #(.trigger("falling")) t_ff_3 (
    .clk(dir[0]), .T(1'b1), .Q(dir[1]), .reset(reset10));  // open: Qn, preset, en
  T_Flip_Flop #(.trigger("falling")) t_ff_4 (.clk(esq[0]), .T(1'b1), .Q(esq[1]), .reset(prox));  // open: Qn, preset, en
  T_Flip_Flop #(.trigger("falling")) t_ff_5 (
    .clk(dir[1]), .T(1'b1), .Q(dir[2]), .reset(reset10));  // open: Qn, preset, en
  T_Flip_Flop #(.trigger("falling")) t_ff_6 (.clk(esq[1]), .T(1'b1), .Q(esq[2]), .reset(prox));  // open: Qn, preset, en
  T_Flip_Flop #(.trigger("falling")) t_ff_7 (
    .clk(dir[2]), .T(1'b1), .Q(dir[3]), .reset(reset10));  // open: Qn, preset, en
  T_Flip_Flop #(.trigger("falling")) t_ff_8 (.clk(esq[2]), .T(1'b1), .Q(esq[3]), .reset(prox));  // open: Qn, preset, en
  and and_1 (reset10, dir[0], ~dir[1], dir[2], ~dir[3]);  // AND_Gate
  and and_2 (prox, esq[0], esq[1], esq[2], ~esq[3]);  // AND_Gate

  // Other names for the same wires on the sheet: b0_t = dir[0]; dist1[3:0] = dir; b1_t = dir[1]; b2_t = dir[2];
  //   b3_t = dir[3]; B0 = esq[0]; dist2[3:0] = esq; B1 = esq[1]; B2 = esq[2]; B3 = esq[3]; reset6 = prox
endmodule
