// Logisim project lookahead.circ as structural Verilog: 3 circuits, main circuit main
module main (
  input  [7:0] A,
  input  [7:0] B,
  input  Operacao,
  output out_4,
  output [7:0] out_5
);

  wire and_1_out, and_2_out, and_3_out, and_4_out, and_5_out, and_6_out, and_7_out, and_8_out, and_9_out,
       and_10_out, and_11_out, and_12_out, and_13_out, and_14_out, and_15_out, and_16_out, and_17_out,
       and_18_out, and_19_out, and_20_out, and_21_out, and_22_out, and_23_out, and_24_out, and_25_out,
       and_26_out, and_27_out, and_28_out, and_29_out, and_30_out, and_31_out, and_32_out, and_33_out,
       and_34_out, and_35_out, and_36_out, G0_out, G1_out, G2_out, G3_out, G4_out, G5_out, G6_out, G7_out,
       operacao_1__1b, or_1_out, or_3_out, or_4_out, or_5_out, or_6_out, or_7_out, or_8_out, or_9_out,
       or_10_out, or_11_out, or_12_out, or_13_out, or_14_out, or_15_out, P0_out, P1_out, P2_out, P3_out,
       P4_out, P5_out, P6_out, P7_out, somador_8_cout;
  wire [7:0] operacao_1_out_3, xor_1_out;

  assign xor_1_out = B ^ operacao_1_out_3;  // XOR_Gate xor_1, 8 bits wide
  operacao operacao_1 (.Op(Operacao), .out_3(operacao_1_out_3), ._1b(operacao_1__1b));
  and and_1 (and_1_out, operacao_1__1b, P0_out, P1_out, P2_out, P3_out, P4_out, P5_out, P6_out, P7_out);
  and and_2 (and_2_out, G0_out, P1_out, P2_out, P3_out, P4_out, P5_out, P6_out, P7_out);
  and and_3 (and_3_out, G1_out, P2_out, P3_out, P4_out, P5_out, P6_out, P7_out);
  and and_4 (and_4_out, G2_out, P3_out, P4_out, P5_out, P6_out, P7_out);
  and and_5 (and_5_out, G3_out, P4_out, P5_out, P6_out, P7_out);
  and and_6 (and_6_out, G4_out, P5_out, P6_out, P7_out);
  or P7 (P7_out, A[7], xor_1_out[7]);
  and and_7 (and_7_out, G6_out, P7_out);
  and and_8 (and_8_out, G5_out, P6_out, P7_out);
  or or_1 (or_1_out, and_1_out, and_2_out, and_3_out, and_4_out, and_5_out, and_6_out, and_8_out, and_7_out);
  and G7 (G7_out, A[7], xor_1_out[7]);
  or or_2 (out_4, or_1_out, G7_out);
  somador somador_1 (.S(out_5[7]), .A(A[7]), .B(xor_1_out[7]), .Cin(or_4_out));  // open: Cout
  and and_9 (and_9_out, operacao_1__1b, P0_out, P1_out, P2_out, P3_out, P4_out, P5_out, P6_out);
  and and_10 (and_10_out, G0_out, P1_out, P2_out, P3_out, P4_out, P5_out, P6_out);
  and and_11 (and_11_out, G1_out, P2_out, P3_out, P4_out, P5_out, P6_out);
  and and_12 (and_12_out, G2_out, P3_out, P4_out, P5_out, P6_out);
  and and_13 (and_13_out, G3_out, P4_out, P5_out, P6_out);
  and and_14 (and_14_out, G4_out, P6_out);
  or P6 (P6_out, A[6], xor_1_out[6]);
  and and_15 (and_15_out, G5_out, P6_out);
  or or_3 (or_3_out, and_9_out, and_10_out, and_11_out, and_12_out, and_13_out, and_14_out, and_15_out);
  or or_4 (or_4_out, or_3_out, G6_out);
  and G6 (G6_out, A[6], xor_1_out[6]);
  somador somador_2 (.S(out_5[6]), .A(A[6]), .B(xor_1_out[6]), .Cin(or_6_out));  // open: Cout
  and and_16 (and_16_out, operacao_1__1b, P0_out, P1_out, P2_out, P3_out, P4_out, P5_out);
  and and_17 (and_17_out, G0_out, P1_out, P2_out, P3_out, P4_out, P5_out);
  and and_18 (and_18_out, G2_out, P3_out, P4_out, P5_out);
  and and_19 (and_19_out, G1_out, P2_out, P3_out, P4_out, P5_out);
  and and_20 (and_20_out, G3_out, P5_out);
  and and_21 (and_21_out, G4_out, P5_out);
  or or_5 (or_5_out, and_16_out, and_17_out, and_19_out, and_18_out, and_20_out, and_21_out);
  and G5 (G5_out, A[5], xor_1_out[5]);
  or P5 (P5_out, A[5], xor_1_out[5]);
  or or_6 (or_6_out, or_5_out, G5_out);
  somador somador_3 (.S(out_5[5]), .A(A[5]), .B(xor_1_out[5]), .Cin(or_8_out));  // open: Cout
  and and_22 (and_22_out, operacao_1__1b, P0_out, P1_out, P2_out, P3_out, P4_out);
  and and_23 (and_23_out, G0_out, P1_out, P2_out, P3_out, P4_out);
  and and_24 (and_24_out, G1_out, P2_out, P3_out, P4_out);
  and and_25 (and_25_out, G2_out, P4_out);
  or P4 (P4_out, A[4], xor_1_out[4]);
  and and_26 (and_26_out, G3_out, P4_out);
  or or_7 (or_7_out, and_22_out, and_23_out, and_24_out, and_25_out, and_26_out);
  or or_8 (or_8_out, or_7_out, G4_out);
  and G4 (G4_out, A[4], xor_1_out[4]);
  somador somador_4 (.S(out_5[4]), .A(A[4]), .B(xor_1_out[4]), .Cin(or_10_out));  // open: Cout
  and and_27 (and_27_out, G0_out, P1_out, P2_out, P3_out);
  and and_28 (and_28_out, operacao_1__1b, P0_out, P1_out, P2_out, P3_out);
  and and_29 (and_29_out, G2_out, P3_out);
  and and_30 (and_30_out, G1_out, P3_out);
  or or_9 (or_9_out, and_28_out, and_27_out, and_30_out, and_29_out);
  and G3 (G3_out, A[3], xor_1_out[3]);
  or P3 (P3_out, A[3], xor_1_out[3]);
  or or_10 (or_10_out, or_9_out, G3_out);
  somador somador_5 (.S(out_5[3]), .A(A[3]), .B(xor_1_out[3]), .Cin(or_12_out));  // open: Cout
  and and_31 (and_31_out, operacao_1__1b, P0_out, P1_out, P2_out);
  or P2 (P2_out, A[2], xor_1_out[2]);
  and and_32 (and_32_out, G0_out, P2_out);
  and and_33 (and_33_out, G0_out, P2_out);
  or or_11 (or_11_out, and_31_out, and_33_out, and_32_out);
  and G2 (G2_out, A[2], xor_1_out[2]);
  or or_12 (or_12_out, or_11_out, G2_out);
  and and_34 (and_34_out, operacao_1__1b, P0_out, P1_out);
  or or_13 (or_13_out, and_34_out, and_35_out);
  somador somador_6 (.S(out_5[2]), .A(A[2]), .B(xor_1_out[2]), .Cin(or_14_out));  // open: Cout
  and G1 (G1_out, A[1], xor_1_out[1]);
  or P1 (P1_out, A[1], xor_1_out[1]);
  and and_35 (and_35_out, G0_out, P1_out);
  or or_14 (or_14_out, or_13_out, G1_out);
  or P0 (P0_out, A[0], xor_1_out[0]);
  and and_36 (and_36_out, operacao_1__1b, P0_out);
  somador somador_7 (.S(out_5[1]), .A(A[1]), .B(xor_1_out[1]), .Cin(or_15_out));  // open: Cout
  and G0 (G0_out, A[0], xor_1_out[0]);
  or or_15 (or_15_out, and_36_out, G0_out);
  somador somador_8 (.S(out_5[0]), .Cout(somador_8_cout), .A(A[0]), .B(xor_1_out[0]), .Cin(operacao_1__1b));
endmodule

module somador (
  input  A,
  input  B,
  input  Cin,
  output S,
  output Cout
);

  wire and_1_out, and_2_out, and_3_out, xor_1_out;

  xor xor_1 (xor_1_out, A, B);
  and and_1 (and_1_out, B, Cin);
  and and_2 (and_2_out, A, B);
  and and_3 (and_3_out, A, Cin);
  xor xor_2 (S, xor_1_out, Cin);
  or or_1 (Cout, and_1_out, and_2_out, and_3_out);
endmodule

module operacao (
  input  Op,
  output _1b,
  output [7:0] out_3
);


  assign _1b = Op;
  assign out_3 = {8{Op}};
endmodule
