// Logisim project mult.circ as structural Verilog: 3 circuits, main circuit main
module main (
  input  [7:0] in_1,
  input  [7:0] in_2,
  output [15:0] out_3
);

  wire _1_2, _1_3, _1_4, _1_5, _1_6, _1_7, _1_8, _2_1, _2_2, _2_3, _2_4, _2_5, _2_6, _2_7, _2_8, _3_1, _3_2,
       _3_3, _3_4, _3_5, _3_6, _3_7, _3_8, _4_1, _4_2, _4_3, _4_4, _4_5, _4_6, _4_7, _4_8, _5_1, _5_2, _5_3,
       _5_4, _5_5, _5_6, _5_7, _5_8, _6_1, _6_2, _6_3, _6_4, _6_5, _6_6, _6_7, _6_8, _7_1, _7_2, _7_3, _7_4,
       _7_5, _7_6, _7_7, _7_8, _8_1, _8_2, _8_3, _8_4, _8_5, _8_6, _8_7, _8_8, somador_2_cout, somador_2_s,
       somador_3_cout, somador_3_s, somador_4_cout, somador_5_cout, somador_5_s, somador_6_cout, somador_6_s,
       somador_7_cout, somador_7_s, somador_8_cout, somador_8_s, somador_9_cout, somador_9_s,
       somador_10_cout, somador_11_cout, somador_11_s, somador_12_cout, somador_12_s, somador_13_cout,
       somador_13_s, somador_14_cout, somador_14_s, somador_15_cout, somador_15_s, somador_16_cout,
       somador_16_s, somador_17_cout, somador_18_cout, somador_19_cout, somador_19_s, somador_20_cout,
       somador_20_s, somador_21_cout, somador_21_s, somador_22_cout, somador_22_s, somador_23_cout,
       somador_23_s, somador_24_cout, somador_24_s, somador_25_cout, somador_25_s, somador_26_cout,
       somador_26_s, somador_27_cout, somador_28_cout, somador_28_s, somador_29_cout, somador_29_s,
       somador_30_cout, somador_30_s, somador_31_cout, somador_31_s, somador_32_cout, somador_32_s,
       somador_33_cout, somador_33_s, somador_34_cout, somador_34_s, somador_35_cout, somador_35_s,
       somador_36_cout, somador_37_cout, somador_37_s, somador_38_cout, somador_38_s, somador_39_cout,
       somador_39_s, somador_40_cout, somador_40_s, somador_41_cout, somador_41_s, somador_42_cout,
       somador_42_s, somador_43_cout, somador_43_s, somador_44_cout, somador_44_s, somador_45_cout,
       somador_45_s, somador_46_cout, somador_46_s, somador_47_cout, somador_47_s, somador_48_cout,
       somador_48_s, somador_inc_1_cout, somador_inc_1_s, somador_inc_2_cout, somador_inc_3_cout,
       somador_inc_4_cout, somador_inc_5_cout, somador_inc_6_cout, somador_inc_7_cout, somador_inc_8_cout;

  somador somador_1 (.S(out_3[14]), .Cout(out_3[15]), .A(somador_3_cout), .B(_8_8), .C(somador_4_cout));
  somador somador_2 (.S(somador_2_s), .Cout(somador_2_cout), .A(somador_6_cout), .B(_8_6), .C(somador_7_cout));
  somador somador_3 (.S(somador_3_s), .Cout(somador_3_cout), .A(somador_2_cout), .B(_8_7), .C(somador_8_cout));
  somador somador_4 (.S(out_3[13]), .Cout(somador_4_cout), .A(somador_3_s), .B(_7_8), .C(somador_10_cout));
  somador somador_5 (.S(somador_5_s), .Cout(somador_5_cout), .A(somador_11_cout), .B(_8_4), .C(somador_12_cout));
  somador somador_6 (.S(somador_6_s), .Cout(somador_6_cout), .A(somador_5_cout), .B(_8_5), .C(somador_13_cout));
  somador somador_7 (.S(somador_7_s), .Cout(somador_7_cout), .A(somador_6_s), .B(_7_6), .C(somador_15_cout));
  somador somador_8 (.S(somador_8_s), .Cout(somador_8_cout), .A(somador_2_s), .B(_7_7), .C(somador_9_cout));
  somador somador_9 (.S(somador_9_s), .Cout(somador_9_cout), .A(somador_7_s), .B(_6_7), .C(somador_16_cout));
  somador somador_10 (.S(out_3[12]), .Cout(somador_10_cout), .A(somador_8_s), .B(_6_8), .C(somador_17_cout));
  somador_inc somador_inc_1 (.A(somador_19_cout), .B(_8_2), .S(somador_inc_1_s), .Cout(somador_inc_1_cout));
  somador somador_11 (.S(somador_11_s), .Cout(somador_11_cout), .A(somador_inc_1_cout), .B(_8_3), .C(somador_21_cout));
  somador somador_12 (.S(somador_12_s), .Cout(somador_12_cout), .A(somador_11_s), .B(_7_4), .C(somador_22_cout));
  somador somador_13 (.S(somador_13_s), .Cout(somador_13_cout), .A(somador_5_s), .B(_7_5), .C(somador_14_cout));
  somador somador_14 (.S(somador_14_s), .Cout(somador_14_cout), .A(somador_12_s), .B(_6_5), .C(somador_23_cout));
  somador somador_15 (.S(somador_15_s), .Cout(somador_15_cout), .A(somador_13_s), .B(_6_6), .C(somador_25_cout));
  somador somador_16 (.S(somador_16_s), .Cout(somador_16_cout), .A(somador_15_s), .B(_5_7), .C(somador_26_cout));
  somador somador_17 (.S(out_3[11]), .Cout(somador_17_cout), .A(somador_9_s), .B(_5_8), .C(somador_18_cout));
  somador somador_18 (.S(out_3[10]), .Cout(somador_18_cout), .A(somador_16_s), .B(_4_8), .C(somador_27_cout));
  somador somador_19 (.S(somador_19_s), .Cout(somador_19_cout), .A(_8_1), .B(_7_2), .C(somador_28_cout));
  somador somador_20 (.S(somador_20_s), .Cout(somador_20_cout), .A(somador_19_s), .B(_6_3), .C(somador_29_cout));
  somador somador_21 (.S(somador_21_s), .Cout(somador_21_cout), .A(somador_inc_1_s), .B(_7_3), .C(somador_20_cout));
  somador somador_22 (.S(somador_22_s), .Cout(somador_22_cout), .A(somador_21_s), .B(_6_4), .C(somador_31_cout));
  somador somador_23 (.S(somador_23_s), .Cout(somador_23_cout), .A(somador_22_s), .B(_5_5), .C(somador_32_cout));
  somador somador_24 (.S(somador_24_s), .Cout(somador_24_cout), .A(somador_23_s), .B(_4_6), .C(somador_33_cout));
  somador somador_25 (.S(somador_25_s), .Cout(somador_25_cout), .A(somador_14_s), .B(_5_6), .C(somador_24_cout));
  somador somador_26 (.S(somador_26_s), .Cout(somador_26_cout), .A(somador_25_s), .B(_4_7), .C(somador_34_cout));
  somador somador_27 (.S(out_3[9]), .Cout(somador_27_cout), .A(somador_26_s), .B(_3_8), .C(somador_36_cout));
  somador somador_28 (.S(somador_28_s), .Cout(somador_28_cout), .A(_7_1), .B(_6_2), .C(somador_37_cout));
  somador somador_29 (.S(somador_29_s), .Cout(somador_29_cout), .A(somador_28_s), .B(_5_3), .C(somador_39_cout));
  somador somador_30 (.S(somador_30_s), .Cout(somador_30_cout), .A(somador_29_s), .B(_4_4), .C(somador_40_cout));
  somador somador_31 (.S(somador_31_s), .Cout(somador_31_cout), .A(somador_20_s), .B(_5_4), .C(somador_30_cout));
  somador somador_32 (.S(somador_32_s), .Cout(somador_32_cout), .A(somador_31_s), .B(_4_5), .C(somador_41_cout));
  somador somador_33 (.S(somador_33_s), .Cout(somador_33_cout), .A(somador_32_s), .B(_3_6), .C(somador_43_cout));
  somador somador_34 (.S(somador_34_s), .Cout(somador_34_cout), .A(somador_24_s), .B(_3_7), .C(somador_35_cout));
  somador somador_35 (.S(somador_35_s), .Cout(somador_35_cout), .A(somador_33_s), .B(_2_7), .C(somador_inc_2_cout));
  somador somador_36 (.S(out_3[8]), .Cout(somador_36_cout), .A(somador_34_s), .B(_2_8), .C(somador_inc_3_cout));
  somador somador_37 (.S(somador_37_s), .Cout(somador_37_cout), .A(_6_1), .B(_5_2), .C(somador_38_cout));
  somador somador_38 (.S(somador_38_s), .Cout(somador_38_cout), .A(_5_1), .B(_4_2), .C(somador_44_cout));
  somador somador_39 (.S(somador_39_s), .Cout(somador_39_cout), .A(somador_37_s), .B(_4_3), .C(somador_46_cout));
  somador somador_40 (.S(somador_40_s), .Cout(somador_40_cout), .A(somador_39_s), .B(_3_4), .C(somador_47_cout));
  somador somador_41 (.S(somador_41_s), .Cout(somador_41_cout), .A(somador_30_s), .B(_3_5), .C(somador_42_cout));
  somador somador_42 (.S(somador_42_s), .Cout(somador_42_cout), .A(somador_40_s), .B(_2_5), .C(somador_inc_4_cout));
  somador somador_43 (.S(somador_43_s), .Cout(somador_43_cout), .A(somador_41_s), .B(_2_6), .C(somador_inc_5_cout));
  somador_inc somador_inc_2 (.A(_1_7), .B(somador_43_s), .S(out_3[6]), .Cout(somador_inc_2_cout));
  somador_inc somador_inc_3 (.A(_1_8), .B(somador_35_s), .S(out_3[7]), .Cout(somador_inc_3_cout));
  somador somador_44 (.S(somador_44_s), .Cout(somador_44_cout), .A(_4_1), .B(_3_2), .C(somador_48_cout));
  somador somador_45 (.S(somador_45_s), .Cout(somador_45_cout), .A(somador_44_s), .B(_2_3), .C(somador_inc_6_cout));
  somador somador_46 (.S(somador_46_s), .Cout(somador_46_cout), .A(somador_38_s), .B(_3_3), .C(somador_45_cout));
  somador somador_47 (.S(somador_47_s), .Cout(somador_47_cout), .A(somador_46_s), .B(_2_4), .C(somador_inc_7_cout));
  somador_inc somador_inc_4 (.A(_1_5), .B(somador_47_s), .S(out_3[4]), .Cout(somador_inc_4_cout));
  somador_inc somador_inc_5 (.A(_1_6), .B(somador_42_s), .S(out_3[5]), .Cout(somador_inc_5_cout));
  somador somador_48 (.S(somador_48_s), .Cout(somador_48_cout), .A(_3_1), .B(_2_2), .C(somador_inc_8_cout));
  somador_inc somador_inc_6 (.A(_1_3), .B(somador_48_s), .S(out_3[2]), .Cout(somador_inc_6_cout));
  somador_inc somador_inc_7 (.A(_1_4), .B(somador_45_s), .S(out_3[3]), .Cout(somador_inc_7_cout));
  somador_inc somador_inc_8 (.A(_2_1), .B(_1_2), .S(out_3[1]), .Cout(somador_inc_8_cout));
  and and_1 (_8_1, in_1[7], in_2[0]);
  and and_2 (_8_2, in_1[7], in_2[1]);
  and and_3 (_8_3, in_1[7], in_2[2]);
  and and_4 (_8_4, in_1[7], in_2[3]);
  and and_5 (_8_5, in_1[7], in_2[4]);
  and and_6 (_8_6, in_1[7], in_2[5]);
  and and_7 (_8_7, in_1[7], in_2[6]);
  and and_8 (_8_8, in_1[7], in_2[7]);
  and and_9 (_6_1, in_1[5], in_2[0]);
  and and_10 (_7_1, in_1[6], in_2[0]);
  and and_11 (_6_2, in_1[5], in_2[1]);
  and and_12 (_7_2, in_1[6], in_2[1]);
  and and_13 (_7_3, in_1[6], in_2[2]);
  and and_14 (_6_3, in_1[5], in_2[2]);
  and and_15 (_7_4, in_1[6], in_2[3]);
  and and_16 (_6_4, in_1[5], in_2[3]);
  and and_17 (_7_5, in_1[6], in_2[4]);
  and and_18 (_6_5, in_1[5], in_2[4]);
  and and_19 (_7_6, in_1[6], in_2[5]);
  and and_20 (_6_6, in_1[5], in_2[5]);
  and and_21 (_6_7, in_1[5], in_2[6]);
  and and_22 (_7_7, in_1[6], in_2[6]);
  and and_23 (_6_8, in_1[5], in_2[7]);
  and and_24 (_7_8, in_1[6], in_2[7]);
  and and_25 (_3_1, in_1[2], in_2[0]);
  and and_26 (_5_1, in_1[4], in_2[0]);
  and and_27 (_4_1, in_1[3], in_2[0]);
  and and_28 (_3_2, in_1[2], in_2[1]);
  and and_29 (_5_2, in_1[4], in_2[1]);
  and and_30 (_4_2, in_1[3], in_2[1]);
  and and_31 (_3_3, in_1[2], in_2[2]);
  and and_32 (_5_3, in_1[4], in_2[2]);
  and and_33 (_4_3, in_1[3], in_2[2]);
  and and_34 (_3_4, in_1[2], in_2[3]);
  and and_35 (_4_4, in_1[3], in_2[3]);
  and and_36 (_5_4, in_1[4], in_2[3]);
  and and_37 (_5_5, in_1[4], in_2[4]);
  and and_38 (_4_5, in_1[3], in_2[4]);
  and and_39 (_3_5, in_1[2], in_2[4]);
  and and_40 (_3_6, in_1[2], in_2[5]);
  and and_41 (_4_6, in_1[3], in_2[5]);
  and and_42 (_5_6, in_1[4], in_2[5]);
  and and_43 (_5_7, in_1[4], in_2[6]);
  and and_44 (_3_7, in_1[2], in_2[6]);
  and and_45 (_4_7, in_1[3], in_2[6]);
  and and_46 (_5_8, in_1[4], in_2[7]);
  and and_47 (_3_8, in_1[2], in_2[7]);
  and and_48 (_4_8, in_1[3], in_2[7]);
  and and_49 (_2_1, in_1[1], in_2[0]);
  and and_50 (out_3[0], in_1[0], in_2[0]);
  and and_51 (_2_2, in_1[1], in_2[1]);
  and and_52 (_1_2, in_1[0], in_2[1]);
  and and_53 (_2_3, in_1[1], in_2[2]);
  and and_54 (_1_3, in_1[0], in_2[2]);
  and and_55 (_2_4, in_1[1], in_2[3]);
  and and_56 (_1_4, in_1[0], in_2[3]);
  and and_57 (_1_5, in_1[0], in_2[4]);
  and and_58 (_2_5, in_1[1], in_2[4]);
  and and_59 (_2_6, in_1[1], in_2[5]);
  and and_60 (_1_6, in_1[0], in_2[5]);
  and and_61 (_1_7, in_1[0], in_2[6]);
  and and_62 (_2_7, in_1[1], in_2[6]);
  and and_63 (_2_8, in_1[1], in_2[7]);
  and and_64 (_1_8, in_1[0], in_2[7]);

  // Other names for the same wires on the sheet: _1_1 = out_3[0]; Res[15:0] = out_3
endmodule

module somador_inc (
  input  A,
  input  B,
  output S,
  output Cout
);

  xor xor_1 (S, A, B);
  and and_1 (Cout, A, B);
endmodule

module somador (
  input  A,
  input  B,
  input  C,
  output S,
  output Cout
);

  wire and_1_out, and_2_out, and_3_out, xor_1_out;

  xor xor_1 (xor_1_out, A, B);
  and and_1 (and_1_out, A, B);
  and and_2 (and_2_out, A, C);
  and and_3 (and_3_out, B, C);
  xor xor_2 (S, xor_1_out, C);
  or or_1 (Cout, and_1_out, and_2_out, and_3_out);
endmodule
