// Logisim project somador_subtrator.circ as structural Verilog: 2 circuits, main circuit main
module main (
  input  [7:0] in_1,
  input  [7:0] in_2,
  input  in_3,
  output out_4,
  output [7:0] out_5
);

  wire somador_2_cout, somador_3_cout, somador_4_cout, somador_5_cout, somador_6_cout, somador_7_cout,
       somador_8_cout, xor_1_out, xor_2_out, xor_3_out, xor_4_out, xor_5_out, xor_6_out, xor_7_out, xor_8_out;

  xor xor_1 (xor_1_out, in_3, in_2[7]);
  somador somador_1 (.S(out_5[7]), .Cout(out_4), .A(in_1[7]), .B(xor_1_out), .Cin(somador_2_cout));
  xor xor_2 (xor_2_out, in_3, in_2[6]);
  somador somador_2 (.S(out_5[6]), .Cout(somador_2_cout), .A(in_1[6]), .B(xor_2_out), .Cin(somador_3_cout));
  xor xor_3 (xor_3_out, in_3, in_2[5]);
  xor xor_4 (xor_4_out, in_3, in_2[4]);
  somador somador_3 (.S(out_5[5]), .Cout(somador_3_cout), .A(in_1[5]), .B(xor_3_out), .Cin(somador_4_cout));
  somador somador_4 (.S(out_5[4]), .Cout(somador_4_cout), .A(in_1[4]), .B(xor_4_out), .Cin(somador_5_cout));
  xor xor_5 (xor_5_out, in_3, in_2[3]);
  somador somador_5 (.S(out_5[3]), .Cout(somador_5_cout), .A(in_1[3]), .B(xor_5_out), .Cin(somador_6_cout));
  xor xor_6 (xor_6_out, in_3, in_2[2]);
  somador somador_6 (.S(out_5[2]), .Cout(somador_6_cout), .A(in_1[2]), .B(xor_6_out), .Cin(somador_7_cout));
  xor xor_7 (xor_7_out, in_3, in_2[1]);
  xor xor_8 (xor_8_out, in_3, in_2[0]);
  somador somador_7 (.S(out_5[1]), .Cout(somador_7_cout), .A(in_1[1]), .B(xor_7_out), .Cin(somador_8_cout));
  somador somador_8 (.S(out_5[0]), .Cout(somador_8_cout), .A(in_1[0]), .B(xor_8_out), .Cin(in_3));
endmodule

module somador (
  input  A,
  input  B,
  input  Cin,
  output S,
  output Cout
);

  wire and_1_out, and_2_out, and_3_out, xor_1_out;

  xor xor_1 (xor_1_out, A, B);
  and and_1 (and_1_out, B, Cin);
  and and_2 (and_2_out, A, B);
  and and_3 (and_3_out, A, Cin);
  xor xor_2 (S, xor_1_out, Cin);
  or or_1 (Cout, and_1_out, and_2_out, and_3_out);
endmodule
