// Logisim project subtrator.circ as structural Verilog: 2 circuits, main circuit main
module main (
  input  [7:0] in_1,
  input  [7:0] in_2,
  output out_3,
  output [7:0] out_4
);

  wire somador_2_cout, somador_3_cout, somador_4_cout, somador_5_cout, somador_6_cout, somador_7_cout,
       somador_8_cout;

  somador somador_1 (.S(out_4[7]), .Cout(out_3), .A(in_1[7]), .B(in_2[7]), .Cin(somador_2_cout));
  somador somador_2 (.S(out_4[6]), .Cout(somador_2_cout), .A(in_1[6]), .B(in_2[6]), .Cin(somador_3_cout));
  somador somador_3 (.S(out_4[5]), .Cout(somador_3_cout), .A(in_1[5]), .B(in_2[5]), .Cin(somador_4_cout));
  somador somador_4 (.S(out_4[4]), .Cout(somador_4_cout), .A(in_1[4]), .B(in_2[4]), .Cin(somador_5_cout));
  somador somador_5 (.S(out_4[3]), .Cout(somador_5_cout), .A(in_1[3]), .B(in_2[3]), .Cin(somador_6_cout));
  somador somador_6 (.S(out_4[2]), .Cout(somador_6_cout), .A(in_1[2]), .B(in_2[2]), .Cin(somador_8_cout));
  somador somador_7 (.S(out_4[0]), .Cout(somador_7_cout), .A(in_1[0]), .B(in_2[0]), .Cin(1'b0));
  somador somador_8 (.S(out_4[1]), .Cout(somador_8_cout), .A(in_1[1]), .B(in_2[1]), .Cin(somador_7_cout));
endmodule

module somador (
  input  A,
  input  B,
  input  Cin,
  output S,
  output Cout
);

  wire and_1_out, and_2_out, and_3_out, xor_1_out;

  xor xor_1 (xor_1_out, A, B);
  and and_1 (and_1_out, B, Cin);
  and and_2 (and_2_out, ~A, B);  // AND_Gate
  and and_3 (and_3_out, ~A, Cin);  // AND_Gate
  xor xor_2 (S, xor_1_out, Cin);
  or or_1 (Cout, and_1_out, and_2_out, and_3_out);
endmodule
